# Fritzing sketch schematic-nodes (saved by Fritzing 0.9.3b)

parts:
  MH-ET_LIVE_ESP32_DEVKIT1 = MH-ET LIVE ESP32 DEVKIT 38 pins
  M1 = MAX485 Breakout [package=THT]
  433T30D1 = 433T30D
  R1 = Resistor [tolerance=±5% resistance=1.6k package="2512 [SMD]"]
  R2 = Resistor [tolerance=±5% resistance=1.6k package="2512 [SMD]"]
  R3 = Resistor [tolerance=±5% resistance=1.6k package="2512 [SMD]"]
  C1 = Electrolytic Capacitor [capacitance=22µF voltage=16V package="0405 [SMD, electrolytic]"]

nets:
  VCC: MH-ET_LIVE_ESP32_DEVKIT1.5V, M1.VCC, 433T30D1.VCC, R1.Pin_1, R2.Pin_1, R3.Pin_1, C1.+
  GND: MH-ET_LIVE_ESP32_DEVKIT1.GND, M1.GND, 433T30D1.GND, C1.-
  N1: MH-ET_LIVE_ESP32_DEVKIT1.IO23, M1.DI
  N2: MH-ET_LIVE_ESP32_DEVKIT1.IO22, M1.RO
  N3: MH-ET_LIVE_ESP32_DEVKIT1.IO21, 433T30D1.AUX
  N4: MH-ET_LIVE_ESP32_DEVKIT1.IO19, 433T30D1.M0
  N5: MH-ET_LIVE_ESP32_DEVKIT1.IO18, 433T30D1.M1
  N6: MH-ET_LIVE_ESP32_DEVKIT1.IO17, 433T30D1.RXD
  N7: MH-ET_LIVE_ESP32_DEVKIT1.IO16, 433T30D1.TXD, R1.Pin_0
  N8: MH-ET_LIVE_ESP32_DEVKIT1.IO4, M1.RE, M1.DE

custom parts:
  MH-ET LIVE ESP32 DEVKIT 38 pins: http://mh.nodebb.com/topic/2/mh-et-live-esp32-devkit
  MAX485 Breakout: MAX485 RS485 breakout board
  433T30D: Long Distance Wireless Transceiver UART LoRa Module
